// Logisim project CPU.circ as structural Verilog: 13 circuits, main circuit IF/ID
module main (
);

  wire branch_control_1_isbranchtaken, control_1_branch, control_1_is_ld_sw, control_1_jump,
       control_1_memread, control_1_memwrite, control_1_out_8, control_1_pop, control_1_push,
       control_1_writeback, ex_mem_1_memread, ex_mem_1_memwrite, ex_mem_1_writeback, hazard_control_1_out_3,
       id_ex_1_branch, id_ex_1_is_ld_sw, id_ex_1_jump, id_ex_1_memread, id_ex_1_memwrite, id_ex_1_out_24,
       id_ex_1_out_25, id_ex_1_pop, id_ex_1_writeback, mem_wb_1_memread, mem_wb_1_writeback, not_1_out,
       or_1_out;
  wire [1:0] forwarding_unit_1_out_7, forwarding_unit_1_out_8;
  wire [2:0] ex_mem_1_rdst_num, id_ex_1_rdst_num, id_ex_1_rsrc_num, ir_decoder_1_rdst_num,
       ir_decoder_1_rsrc_num, mem_wb_1_rdst_num, undriven_2;
  wire [4:0] id_ex_1_opcode, ir_decoder_1_opcode;
  wire [15:0] id_ex_1_immediate, ir_decoder_1_immediate;
  wire [31:0] alu_1_result, bit_extender_1_out, branch_control_1_pc_out, ex_mem_1_alu_out,
       ex_mem_1_rdst_data, id_ex_1_rdst_data, id_ex_1_rsrc_data, if_id_1_out_3, mem_wb_1_alu_out,
       mem_wb_1_memorydata, multiplexer_1_out, multiplexer_2_out, multiplexer_3_out, multiplexer_4_out,
       multiplexer_5_out, PC_q, ram_1_read_data, ram_2_read_data, regfile_1_rdst_out, regfile_1_rsrc_out,
       undriven;

  Hazard_Control hazard_control_1 (.CurrentIR(if_id_1_out_3), .NextIR(ram_1_read_data), .out_3(hazard_control_1_out_3));
  not not_1 (not_1_out, hazard_control_1_out_3);
  Register #(.width(32)) PC (.D(branch_control_1_pc_out), .en(not_1_out), .Q(PC_q));  // open: clk, clr
  RAM ram_1 (.Memory_Read(1'b1), .Memory_Write(1'b0), .Address(PC_q), .Read_Data(ram_1_read_data));  // open: Write_Data
  IF_ID if_id_1 (.in_1(ram_1_read_data), .out_3(if_id_1_out_3), .Reset(or_1_out));
  or or_1 (or_1_out, hazard_control_1_out_3, branch_control_1_isbranchtaken);
  IR_Decoder ir_decoder_1 (
    .IR(if_id_1_out_3), .OpCode(ir_decoder_1_opcode), .Rsrc_num(ir_decoder_1_rsrc_num),
    .Rdst_num(ir_decoder_1_rdst_num), .Immediate(ir_decoder_1_immediate));
  Control control_1 (
    .MemRead(control_1_memread), .MemWrite(control_1_memwrite), .Branch(control_1_branch),
    .WriteBack(control_1_writeback), .IR(if_id_1_out_3), .out_8(control_1_out_8), .PUSH(control_1_push),
    .Jump(control_1_jump), .POP(control_1_pop), .is_ld_sw(control_1_is_ld_sw));
  Regfile regfile_1 (
    .Rsrc_num(ir_decoder_1_rsrc_num), .Rdst_num_2(ir_decoder_1_rdst_num), .Rsrc_out(regfile_1_rsrc_out),
    .Rdst_out(regfile_1_rdst_out), .Rdst_enable(mem_wb_1_writeback), .Datain(multiplexer_5_out),
    .Rdst_num(mem_wb_1_rdst_num));
  ID_EX id_ex_1 (
    .MemRead(id_ex_1_memread), .MemWrite(id_ex_1_memwrite), .WriteBack(id_ex_1_writeback),
    .Branch(id_ex_1_branch), .in_2(control_1_memread), .in_7(control_1_branch), .in_5(control_1_writeback),
    .in_3(control_1_memwrite), .Rdst_num(id_ex_1_rdst_num), .in_13(ir_decoder_1_rdst_num),
    .in_12(ir_decoder_1_rsrc_num), .Rsrc_num(id_ex_1_rsrc_num), .in_14(regfile_1_rsrc_out),
    .Rsrc_data(id_ex_1_rsrc_data), .in_15(regfile_1_rdst_out), .Rdst_data(id_ex_1_rdst_data),
    .in_16(ir_decoder_1_immediate), .Immediate(id_ex_1_immediate), .in_11(ir_decoder_1_opcode),
    .OPCode(id_ex_1_opcode), .Jump(id_ex_1_jump), .out_24(id_ex_1_out_24), .out_25(id_ex_1_out_25),
    .in_8(control_1_jump), .in_9(control_1_out_8), .push(control_1_push),
    .RST(branch_control_1_isbranchtaken), .in_6(control_1_pop), .pop(id_ex_1_pop), .in_4(control_1_is_ld_sw),
    .is_ld_sw(id_ex_1_is_ld_sw));
  Forwarding_Unit forwarding_unit_1 (
    .in_1(id_ex_1_rdst_num), .in_3(ex_mem_1_writeback), .in_4(mem_wb_1_writeback), .in_5(mem_wb_1_rdst_num),
    .in_6(ex_mem_1_rdst_num), .out_7(forwarding_unit_1_out_7), .in_2(id_ex_1_rsrc_num),
    .out_8(forwarding_unit_1_out_8));
  Multiplexer #(.select(2), .width(32), .enable("false")) multiplexer_1 (
    .in1(ex_mem_1_alu_out), .in2(multiplexer_5_out), .in3(id_ex_1_rsrc_data), .out(multiplexer_1_out),
    .sel(forwarding_unit_1_out_7));  // open: in0
  Multiplexer #(.select(2), .width(32), .enable("false")) multiplexer_2 (
    .in1(ex_mem_1_alu_out), .in2(multiplexer_5_out), .in3(id_ex_1_rdst_data), .out(multiplexer_2_out),
    .sel(forwarding_unit_1_out_8));  // open: in0
  assign bit_extender_1_out = {{16{id_ex_1_immediate[15]}}, id_ex_1_immediate};  // Bit_Extender bit_extender_1
  Multiplexer #(.width(32), .enable("false")) multiplexer_3 (
    .in0(multiplexer_1_out), .in1(bit_extender_1_out), .out(multiplexer_3_out), .sel(id_ex_1_out_24));
  Multiplexer #(.width(32), .enable("false")) multiplexer_4 (
    .in0(multiplexer_2_out), .in1(multiplexer_1_out), .out(multiplexer_4_out), .sel(id_ex_1_is_ld_sw));
  ALU alu_1 (
    .dst(multiplexer_4_out), .Selection(id_ex_1_opcode), .Result(alu_1_result), .Flags(undriven_2),
    .src(multiplexer_3_out), .push(id_ex_1_out_25), .pop(id_ex_1_pop), .in_4(undriven));
  Branch_Control branch_control_1 (
    .Branch(id_ex_1_branch), .Jump(id_ex_1_jump), .OPCode(id_ex_1_opcode), .Flags(undriven_2), .PC_In(PC_q),
    .Has_Next_Operand(id_ex_1_out_24), .Rdst_Address(multiplexer_2_out), .PC_Out(branch_control_1_pc_out),
    .isBranchTaken(branch_control_1_isbranchtaken));
  EX_MEM ex_mem_1 (
    .in_1(id_ex_1_memread), .MemRead(ex_mem_1_memread), .in_2(id_ex_1_memwrite),
    .MemWrite(ex_mem_1_memwrite), .in_3(id_ex_1_writeback), .WriteBack(ex_mem_1_writeback),
    .in_4(alu_1_result), .ALU_Out(ex_mem_1_alu_out), .in_6(id_ex_1_rdst_num), .Rdst_num(ex_mem_1_rdst_num),
    .in_5(multiplexer_2_out), .Rdst_data(ex_mem_1_rdst_data));
  RAM ram_2 (
    .Memory_Read(ex_mem_1_memread), .Memory_Write(ex_mem_1_memwrite), .Address(ex_mem_1_alu_out),
    .Write_Data(ex_mem_1_rdst_data), .Read_Data(ram_2_read_data));
  MEM_WB mem_wb_1 (
    .in_1(ex_mem_1_memread), .MemRead(mem_wb_1_memread), .in_2(ex_mem_1_writeback),
    .WriteBack(mem_wb_1_writeback), .in_4(ex_mem_1_alu_out), .ALU_Out(mem_wb_1_alu_out),
    .in_5(ex_mem_1_rdst_num), .Rdst_num(mem_wb_1_rdst_num), .in_3(ram_2_read_data),
    .MemoryData(mem_wb_1_memorydata));
  Multiplexer #(.width(32), .enable("false")) multiplexer_5 (
    .in0(mem_wb_1_alu_out), .in1(mem_wb_1_memorydata), .out(multiplexer_5_out), .sel(mem_wb_1_memread));

  // Notes on the sheet:
  //   ***Negative Edges***
  //   Rsrc
  //   Rdst
  //   5 Stage Pipelined 32 bit Harvard Processor
endmodule

module Control (
  input  [31:0] IR,
  output is_ld_sw,
  output MemRead,
  output MemWrite,
  output WriteBack,
  output Branch,
  output Jump,
  output out_8,
  output PUSH,
  output POP
);

  wire and_1_out, and_2_out, and_5_out, nor_1_out;

  and and_1 (and_1_out, IR[31], IR[30], ~IR[29], IR[28]);  // AND_Gate
  and and_2 (and_2_out, IR[31], ~IR[30], IR[29], ~IR[28]);  // AND_Gate
  nor nor_1 (nor_1_out, IR[25], IR[24], IR[23]);
  or or_1 (is_ld_sw, and_1_out, and_2_out);
  and and_3 (Branch, IR[27], IR[26]);
  and and_4 (Jump, Branch, nor_1_out);
  and and_5 (and_5_out, ~IR[27], IR[26], ~IR[24], IR[25]);  // AND_Gate
  and and_6 (PUSH, ~IR[23], and_5_out);  // AND_Gate
  and and_7 (POP, IR[23], and_5_out);

  assign MemRead = IR[30];
  assign MemWrite = IR[29];
  assign out_8 = IR[31];
  assign WriteBack = IR[28];

  // Notes on the sheet:
  //   Has Next Operand
endmodule

module IF_ID (
  input  [31:0] in_1,
  input  Reset,
  output [31:0] out_3
);

  Register #(.width(32)) register_1 (.D(in_1), .Q(out_3), .clr(Reset));  // open: en, clk

  // Notes on the sheet:
  //   IR
  //   IR
endmodule

module ID_EX (
  input  RST,
  input  in_2,
  input  in_3,
  input  in_4,
  input  in_5,
  input  in_6,
  input  in_7,
  input  in_8,
  input  in_9,
  input  push,
  input  [4:0] in_11,
  input  [2:0] in_12,
  input  [2:0] in_13,
  input  [31:0] in_14,
  input  [31:0] in_15,
  input  [15:0] in_16,
  output MemRead,
  output MemWrite,
  output is_ld_sw,
  output WriteBack,
  output pop,
  output Branch,
  output Jump,
  output out_24,
  output out_25,
  output [4:0] OPCode,
  output [2:0] Rsrc_num,
  output [2:0] Rdst_num,
  output [31:0] Rsrc_data,
  output [31:0] Rdst_data,
  output [15:0] Immediate
);


  assign Branch = in_7;
  assign Immediate = in_16;
  assign is_ld_sw = in_4;
  assign Jump = in_8;
  assign MemRead = in_2;
  assign MemWrite = in_3;
  assign OPCode = in_11;
  assign out_24 = in_9;
  assign out_25 = push;
  assign pop = in_6;
  assign Rdst_data = in_15;
  assign Rdst_num = in_13;
  assign Rsrc_data = in_14;
  assign Rsrc_num = in_12;
  assign WriteBack = in_5;

  // Notes on the sheet:
  //   Has Next Operand
endmodule

module EX_MEM (
  input  in_1,
  input  in_2,
  input  in_3,
  input  [31:0] in_4,
  input  [31:0] in_5,
  input  [2:0] in_6,
  output MemRead,
  output MemWrite,
  output WriteBack,
  output [31:0] ALU_Out,
  output [31:0] Rdst_data,
  output [2:0] Rdst_num
);


  assign ALU_Out = in_4;
  assign MemRead = in_1;
  assign MemWrite = in_2;
  assign Rdst_data = in_5;
  assign Rdst_num = in_6;
  assign WriteBack = in_3;
endmodule

module MEM_WB (
  input  in_1,
  input  in_2,
  input  [31:0] in_3,
  input  [31:0] in_4,
  input  [2:0] in_5,
  output MemRead,
  output WriteBack,
  output [31:0] MemoryData,
  output [31:0] ALU_Out,
  output [2:0] Rdst_num
);


  assign ALU_Out = in_4;
  assign MemoryData = in_3;
  assign MemRead = in_1;
  assign Rdst_num = in_5;
  assign WriteBack = in_2;
endmodule

module Regfile (
  input  [2:0] Rsrc_num,
  input  Rdst_enable,
  input  [2:0] Rdst_num,
  input  [31:0] Datain,
  input  [2:0] Rdst_num_2,
  output [31:0] Rsrc_out,
  output [31:0] Rdst_out
);

  wire decoder_1_out0, decoder_1_out1, decoder_1_out2, decoder_1_out3, decoder_1_out4, decoder_1_out5,
       decoder_1_out6, decoder_1_out7;
  wire [31:0] register_1_q, register_2_q, register_3_q, register_4_q, register_5_q, register_6_q,
       register_7_q, register_8_q;

  Decoder #(.select(3), .disabled(0)) decoder_1 (
    .out0(decoder_1_out0), .out1(decoder_1_out1), .out2(decoder_1_out2), .out3(decoder_1_out3),
    .out4(decoder_1_out4), .out5(decoder_1_out5), .out6(decoder_1_out6), .out7(decoder_1_out7),
    .sel(Rdst_num), .en(Rdst_enable));
  Register #(.width(32), .trigger("falling")) register_1 (
    .D(Datain), .en(decoder_1_out0), .Q(register_1_q));  // open: clk, clr
  Register #(.width(32), .trigger("falling")) register_2 (
    .D(Datain), .en(decoder_1_out1), .Q(register_2_q));  // open: clk, clr
  Register #(.width(32), .trigger("falling")) register_3 (
    .D(Datain), .en(decoder_1_out2), .Q(register_3_q));  // open: clk, clr
  Register #(.width(32), .trigger("falling")) register_4 (
    .D(Datain), .en(decoder_1_out3), .Q(register_4_q));  // open: clk, clr
  Register #(.width(32), .trigger("falling")) register_5 (
    .D(Datain), .en(decoder_1_out4), .Q(register_5_q));  // open: clk, clr
  Register #(.width(32), .trigger("falling")) register_6 (
    .D(Datain), .en(decoder_1_out5), .Q(register_6_q));  // open: clk, clr
  Register #(.width(32), .trigger("falling")) register_7 (
    .D(Datain), .en(decoder_1_out6), .Q(register_7_q));  // open: clk, clr
  Register #(.width(32), .trigger("falling")) register_8 (
    .D(Datain), .en(decoder_1_out7), .Q(register_8_q));  // open: clk, clr
  Multiplexer #(.select(3), .width(32), .enable("false")) multiplexer_1 (
    .in0(register_1_q), .in1(register_2_q), .in2(register_3_q), .in3(register_4_q), .in4(register_5_q),
    .in5(register_6_q), .in6(register_7_q), .in7(register_8_q), .out(Rsrc_out), .sel(Rsrc_num));
  Multiplexer #(.select(3), .width(32), .enable("false")) multiplexer_2 (
    .in0(register_1_q), .in1(register_2_q), .in2(register_3_q), .in3(register_4_q), .in4(register_5_q),
    .in5(register_6_q), .in6(register_7_q), .in7(register_8_q), .out(Rdst_out), .sel(Rdst_num_2));

  // Notes on the sheet:
  //   ***Registers are falling edges***
endmodule

module ALU (
  input  [31:0] src,
  input  [31:0] dst,
  input  [2:0] Flags,
  input  [31:0] in_4,
  input  push,
  input  pop,
  input  [4:0] Selection,
  output [31:0] Result
);

  wire adder_1_cout, and_2_out, and_3_out, or_1_out, subtractor_1_bout;
  wire [2:0] comparator_1_eq, comparator_2_eq;
  wire [31:0] adder_1_out, adder_2_out, adder_3_out, and_1_out, multiplexer_1_out, multiplexer_2_out,
       multiplexer_3_out, multiplexer_5_out, multiplexer_7_out, multiplexer_9_out, negator_1_out, not_1_out,
       or_2_out, shifter_1_out, shifter_2_out, shifter_3_out, shifter_4_out, SP_q, subtractor_1_out,
       subtractor_2_out, subtractor_3_out;

  Multiplexer #(.width(32), .enable("false")) multiplexer_1 (
    .in0(adder_3_out), .in1(subtractor_3_out), .out(multiplexer_1_out), .sel(push));
  or or_1 (or_1_out, push, pop);
  Register #(.width(32)) SP (.D(multiplexer_1_out), .en(or_1_out), .Q(SP_q));  // open: clk, clr
  Adder #(.width(32)) adder_1 (.a(dst), .b(src), .out(adder_1_out), .cin(1'b0), .cout(adder_1_cout));
  Subtractor #(.width(32)) subtractor_1 (
    .a(dst), .b(src), .out(subtractor_1_out), .bin(1'b0), .bout(subtractor_1_bout));
  assign and_1_out = dst & src;  // AND_Gate and_1, 32 bits wide
  assign or_2_out = dst | src;  // OR_Gate or_2, 32 bits wide
  Shifter #(.width(32)) shifter_1 (.in(dst), .\dist (src[4:0]), .out(shifter_1_out));
  Shifter #(.width(32), .shift("lr")) shifter_2 (.in(dst), .\dist (src[4:0]), .out(shifter_2_out));
  assign not_1_out = ~dst;  // NOT_Gate not_1, 32 bits wide
  Adder #(.width(32)) adder_2 (.a(dst), .b({32{1'b0}}), .out(adder_2_out), .cin(1'b1));  // open: cout
  Subtractor #(.width(32)) subtractor_2 (.a(dst), .b({32{1'b0}}), .out(subtractor_2_out), .bin(1'b1));  // open: bout
  Negator #(.width(32)) negator_1 (.in(dst), .out(negator_1_out));
  Shifter #(.width(32), .shift("rl")) shifter_3 (.in(dst), .\dist (5'b00001), .out(shifter_3_out));
  Shifter #(.width(32), .shift("rr")) shifter_4 (.in(dst), .\dist (5'b00001), .out(shifter_4_out));
  Adder #(.width(32)) adder_3 (.a(SP_q), .b(32'h4), .out(adder_3_out));  // open: cin, cout
  Subtractor #(.width(32)) subtractor_3 (.a(SP_q), .b(32'h4), .out(subtractor_3_out));  // open: bin, bout
  Multiplexer #(.select(2), .width(32), .disabled(0), .enable("false")) multiplexer_2 (
    .in0(adder_1_out), .in1(subtractor_1_out), .in2(and_1_out), .in3(or_2_out), .out(multiplexer_2_out),
    .sel(Selection[1:0]));
  Multiplexer #(.select(3), .width(32), .enable("false")) multiplexer_3 (
    .in0(adder_1_out), .in1(subtractor_1_out), .in2(and_1_out), .in3(or_2_out), .in4(src),
    .in5(shifter_1_out), .in6(shifter_2_out), .out(multiplexer_3_out), .sel(Selection[2:0]));  // open: in7
  Multiplexer #(.select(2), .enable("false")) multiplexer_4 (
    .in0(adder_1_cout), .in1(subtractor_1_bout), .in2(shifter_2_out[0]), .in3(shifter_1_out[0]),
    .out(comparator_1_eq[2]), .sel({Selection[2], Selection[0]}));
  Comparator #(.width(32)) comparator_1 (
    .a({32{1'b0}}), .b(multiplexer_2_out), .gt(comparator_1_eq[1]), .eq(comparator_1_eq[0]));  // open: lt
  Multiplexer #(.select(2), .width(32), .disabled(0), .enable("false")) multiplexer_5 (
    .in0(not_1_out), .in1(adder_2_out), .in2(subtractor_2_out), .in3(negator_1_out), .out(multiplexer_5_out),
    .sel(Selection[1:0]));
  Multiplexer #(.select(2), .enable("false")) multiplexer_6 (
    .in0(1'b0), .in1(1'b1), .in2(shifter_3_out[0]), .in3(shifter_4_out[0]), .out(comparator_2_eq[2]),
    .sel({Selection[3], Selection[0]}));
  Comparator #(.width(32)) comparator_2 (
    .a({32{1'b0}}), .b(multiplexer_5_out), .gt(comparator_2_eq[1]), .eq(comparator_2_eq[0]));  // open: lt
  Multiplexer #(.select(4), .width(32), .enable("false")) multiplexer_7 (
    .in0({32{1'b0}}), .in3({32{1'b0}}), .in4(not_1_out), .in5(adder_2_out), .in6(subtractor_2_out),
    .in7(negator_1_out), .in10(shifter_3_out), .in11(shifter_4_out), .in12(SP_q), .in13(adder_3_out),
    .out(multiplexer_7_out), .sel(Selection[3:0]));  // open: in1, in2, in8, in9, in14, in15
  and and_2 (and_2_out, ~Selection[4], Selection[3], ~Selection[2], ~Selection[1], ~Selection[0]);  // AND_Gate
  Multiplexer #(.width(3), .enable("false")) multiplexer_8 (
    .in0(comparator_2_eq), .in1(comparator_1_eq), .out(Flags), .sel(Selection[4]));
  Multiplexer #(.width(32), .enable("false")) multiplexer_9 (
    .in0(multiplexer_7_out), .in1(multiplexer_3_out), .out(multiplexer_9_out), .sel(Selection[4]));
  Register #(.width(32)) OUT (.D(dst), .en(and_2_out));  // open: Q, clk, clr
  Multiplexer #(.width(32), .enable("false")) multiplexer_10 (
    .in0(multiplexer_9_out), .in1(in_4), .out(Result), .sel(and_3_out));
  and and_3 (and_3_out, ~Selection[4], Selection[3], ~Selection[2], ~Selection[1], Selection[0]);  // AND_Gate

  // Notes on the sheet:
  //   Carry Somewhere
  //   Carry
  //   Carry
  //   Carry Somewhere
  //   Two Operands
  //   One Operand
  //   Carry
  //   Carry
  //   Carry
  //   Carry
  //   push
  //   pop
  //   out
  //   carry
  //   Negative
  //   Zero
  //   Negative
  //   carry
  //   Zero
  //   IN
endmodule

module Forwarding_Unit (
  input  [2:0] in_1,
  input  [2:0] in_2,
  input  in_3,
  input  in_4,
  input  [2:0] in_5,
  input  [2:0] in_6,
  output [1:0] out_7,
  output [1:0] out_8
);


  // Notes on the sheet:
  //   return 1
  //   return 2
  //   else
  //   return 3
  //   return 1
  //   return 2
  //   else
  //   return 3
  //   If EX/Mem.WriteBack && (EX/Mem.RegDst == ID/Ex.RegSrc) 
  //   else If Mem/Wb.WriteBack && (Mem/Wb.RegDst == ID/Ex.RegSrc) 
  //   If EX/Mem.WriteBack && (EX/Mem.RegDst == ID/Ex.RegDst) 
  //   else If Mem/Wb.WriteBack && (Mem/Wb.RegDst == ID/Ex.RegDst) 
  //   // Has Higher Priority
  //   // Has Higher Priority
endmodule

module IR_Decoder (
  input  [31:0] IR,
  output [15:0] Immediate,
  output [2:0] Rsrc_num,
  output [2:0] Rdst_num,
  output [4:0] OpCode
);


  assign Immediate = IR[15:0];
  assign OpCode = IR[26:22];
  assign Rdst_num = IR[21:19];
  assign Rsrc_num = IR[18:16];
endmodule

module RAM (
  input  [31:0] Write_Data,
  input  [31:0] Address,
  input  Memory_Read,
  input  Memory_Write,
  output [31:0] Read_Data
);

  wire or_1_out;
  wire [31:0] ram_1_data;

  or or_1 (or_1_out, Memory_Read, Memory_Write);
  RAM_part #(.addrWidth(20), .dataWidth(32)) ram_1 (
    .addr(Address[19:0]), .data(ram_1_data), .sel(or_1_out), .ld(Memory_Read));  // open: clk, clr
  Multiplexer #(.width(32), .enable("false")) multiplexer_1 (
    .in0(Write_Data), .in1(Read_Data), .out(ram_1_data), .sel(Memory_Read));
endmodule

module Branch_Control (
  input  Branch,
  input  Jump,
  input  [4:0] OPCode,
  input  [2:0] Flags,
  input  [31:0] PC_In,
  input  Has_Next_Operand,
  input  [31:0] Rdst_Address,
  output isBranchTaken,
  output [31:0] PC_Out
);

  wire and_1_out, comparator_1_eq;
  wire [2:0] decoder_1_out0;
  wire [31:0] adder_1_out, multiplexer_1_out;

  Decoder #(.select(2), .enable("false")) decoder_1 (
    .out0(decoder_1_out0[0]), .out1(decoder_1_out0[1]), .out2(decoder_1_out0[2]), .sel(OPCode[1:0]));  // open: out3
  Multiplexer #(.width(32), .enable("false")) multiplexer_1 (
    .in0(32'h2), .in1(32'h4), .out(multiplexer_1_out), .sel(Has_Next_Operand));
  Comparator #(.width(3), .mode("unsigned")) comparator_1 (
    .a(decoder_1_out0), .b(Flags), .eq(comparator_1_eq));  // open: gt, lt
  Adder #(.width(32)) adder_1 (.a(PC_In), .b(multiplexer_1_out), .out(adder_1_out), .cin(1'b0));  // open: cout
  and and_1 (and_1_out, Branch, comparator_1_eq);
  or or_1 (isBranchTaken, Jump, and_1_out);
  Multiplexer #(.width(32), .enable("false")) multiplexer_2 (
    .in0(adder_1_out), .in1(Rdst_Address), .out(PC_Out), .sel(isBranchTaken));

  // Notes on the sheet:
  //   000 No Flags
  //   001 Zero
  //   010 Negative
  //   100 Carry
endmodule

module Hazard_Control (
  input  [31:0] CurrentIR,
  input  [31:0] NextIR,
  output out_3
);


  assign out_3 = 1'b0;
endmodule
